# Fritzing sketch esp32Control (saved by Fritzing 0.9.4)

parts:
  Bauteil3 = Adafruit Analog 2-Axis Joystick [part_number="Adafruit #512"]
  Bauteil4 = Adafruit Analog 2-Axis Joystick [part_number="Adafruit #512"]
  LED1 = LED - 3mm [color="Red (633nm)" package="3 mm [THT]"]
  RE1 = Rotary Encoder [package=THT]
  S1 = Toggle Switch [package=THT]
  Mod1 = ESP32-TTGO-T-DISPLAY
  R1 = Resistor [tolerance=±5% resistance=10k package=THT]
  R2 = Resistor [tolerance=±5% resistance=330 package=THT]
  R3 = Resistor [tolerance=±5% resistance=330 package=THT]

nets:
  GND: Bauteil3.GND, Bauteil4.GND, LED1.cathode, RE1.EncoderPinC, Mod1.G-1, Mod1.G-10, Mod1.G-11, Mod1.G-14, Mod1.27, R1.Pin_0
  N1: Bauteil3.SWITCH, Mod1.37
  N2: Bauteil3.YOUT, Mod1.39
  N3: Bauteil3.XOUT, Mod1.36
  VCC: Bauteil3.VCC, Bauteil4.VCC, S1.L1, Mod1.3V
  N4: Bauteil4.SWITCH, Mod1.15
  N5: Bauteil4.YOUT, Mod1.13
  N6: Bauteil4.XOUT, Mod1.12
  N7: LED1.anode, R3.Pin_1
  N8: RE1.EncoderPinA, Mod1.38
  N9: RE1.EncoderPinB, Mod1.32
  N10: S1.L2, R1.Pin_1, R2.Pin_1
  N11: Mod1.17, R3.Pin_0
  N12: Mod1.2, R2.Pin_0

custom parts:
  Adafruit Analog 2-Axis Joystick: This mini-kit makes it easy to mount a PSP/Xbox-like thumb joystick to your project. The thumbstick is an analog joystick - more accurate and sensitive than just 'directional' joysticks - with a 'press in to select' button. Since it's analog, you'll need two analog reading pins on your microcontroller to determine X and Y. Having an extra digital input will let you read the switch. The pack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
  ESP32-TTGO-T-DISPLAY: LILYGO TTGO T-Display GD32VF103CBT6 Main Chip ST7789 1.14 Inch IPS 240x135 Resolution Minimalist Development Board.
