# Fritzing sketch esp32RootServer (saved by Fritzing 0.9.4)

parts:
  Bauteil1 = Adafruit HUZZAH32 ESP32 Feather [part_number="Adafruit #3405"]
  Bauteil2 = Adafruit Adalogger FeatherWing [part_number="Adafruit #2922"]
  C1 = Capacitor Polarized [package=cpol-radial-10uf-25v]

nets:
  N1: Bauteil1.MISO, Bauteil2.MISO
  N2: Bauteil1.MOSI, Bauteil2.MOSI
  N3: Bauteil1.SCK, Bauteil2.SCK
  GND: Bauteil1.GND, Bauteil2.GND, C1.-
  3.3V: Bauteil1.3.3V, Bauteil2.+3V3
  N4: Bauteil1.RESET, Bauteil2.RESET
  N5: Bauteil1.VBAT, Bauteil2.VBAT
  N6: Bauteil1.EN, C1.+
  N7: Bauteil1.IO33_A9, Bauteil2.CS
  N8: Bauteil1.SCL, Bauteil2.SCL
  N9: Bauteil1.SDA, Bauteil2.SDA

custom parts:
  Adafruit Adalogger FeatherWing: This is the Adalogger FeatherWing: it adds both a battery-backed Real Time Clock and micro SD card storage to any Feather main board. This FeatherWing will make it real easy to add datalogging to any of our existing Feathers. You get both an I2C real time clock (PCF8523) with 32KHz crystal and battery backup, and a microSD socket that connects to the SPI port pins (+ extra pin for CS). Tested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
