# Fritzing sketch esp8266DiffDriveChassis (saved by Fritzing 0.9.4)

parts:
  WeMos_D1_Mini1 = WeMos D1 Mini
  WeMos_D1_Mini_Micro_SD_Shield1 = WeMos D1 Mini Micro SD Shield
  WeMos_D1_Mini_Protoboard_Shield1 = WeMos D1 Mini Protoboard Shield
  WeMos_D1_Mini_Protoboard_Shield3 = WeMos D1 Mini Protoboard Shield
  U1 = mystery part, 3 pins [chip_label=?]
  M1 = DC Motor
  M4 = DC Motor  # not connected
  M2 = DC Motor  # not connected
  M3 = DC Motor
  WeMos_D1_Mini_Motor_Shield1 = WeMos D1 Mini Motor Shield

nets:
  3V3: WeMos_D1_Mini1.3V3, WeMos_D1_Mini_Micro_SD_Shield1.3V3, WeMos_D1_Mini_Protoboard_Shield1.3V3, WeMos_D1_Mini_Protoboard_Shield3.3V3
  5V: WeMos_D1_Mini1.5V, WeMos_D1_Mini_Micro_SD_Shield1.5V, WeMos_D1_Mini_Protoboard_Shield1.5V, WeMos_D1_Mini_Protoboard_Shield3.5V, WeMos_D1_Mini_Motor_Shield1.5V
  N1: WeMos_D1_Mini1.D1, WeMos_D1_Mini_Protoboard_Shield1.D1, WeMos_D1_Mini_Motor_Shield1.D1
  N2: WeMos_D1_Mini1.D2, WeMos_D1_Mini_Protoboard_Shield1.D2
  N3: WeMos_D1_Mini1.D5, WeMos_D1_Mini_Micro_SD_Shield1.D5
  N4: WeMos_D1_Mini1.D6, WeMos_D1_Mini_Micro_SD_Shield1.D6
  N5: WeMos_D1_Mini1.D7, WeMos_D1_Mini_Micro_SD_Shield1.D7
  N6: WeMos_D1_Mini1.D8, WeMos_D1_Mini_Micro_SD_Shield1.D8
  N7: WeMos_D1_Mini1.G, WeMos_D1_Mini_Protoboard_Shield1.G, WeMos_D1_Mini_Protoboard_Shield3.G, WeMos_D1_Mini_Motor_Shield1.G
  N8: WeMos_D1_Mini1.RST, WeMos_D1_Mini_Micro_SD_Shield1.RST, WeMos_D1_Mini_Protoboard_Shield1.RST, WeMos_D1_Mini_Protoboard_Shield3.RST
  GND1: WeMos_D1_Mini_Protoboard_Shield3.X8-Y11, U1.pin3, WeMos_D1_Mini_Motor_Shield1.GND1, WeMos_D1_Mini_Motor_Shield1.GND2
  N9: WeMos_D1_Mini_Protoboard_Shield3.X9-Y11, U1.pin2
  N10: U1.pin1, WeMos_D1_Mini_Motor_Shield1.VM1, WeMos_D1_Mini_Motor_Shield1.VM2
  N11: M1.pin_1, WeMos_D1_Mini_Motor_Shield1.B1
  N12: M1.pin_2, WeMos_D1_Mini_Motor_Shield1.B2
  N13: M3.pin_1, WeMos_D1_Mini_Motor_Shield1.A1
  N14: M3.pin_2, WeMos_D1_Mini_Motor_Shield1.A2

notes:
  RTC Shield
  7-24V Power Shield
  GND
  + 7,2 V
  + 9,6 V
  8 Cell NiMH
  Battery Pack with 2 Voltages
