# Fritzing sketch esp8266RootServer (saved by Fritzing 0.9.4)

parts:
  WeMos_D1_Mini1 = WeMos D1 Mini
  WeMos_D1_Mini_Micro_SD_Shield1 = WeMos D1 Mini Micro SD Shield
  WeMos_D1_Mini_OLED_Shield1 = WeMos D1 Mini OLED Shield
  WeMos_D1_Mini_Protoboard_Shield1 = WeMos D1 Mini Protoboard Shield

nets:
  3V3: WeMos_D1_Mini1.3V3, WeMos_D1_Mini_Micro_SD_Shield1.3V3, WeMos_D1_Mini_OLED_Shield1.3V3, WeMos_D1_Mini_Protoboard_Shield1.3V3
  5V: WeMos_D1_Mini1.5V, WeMos_D1_Mini_Micro_SD_Shield1.5V, WeMos_D1_Mini_OLED_Shield1.5V, WeMos_D1_Mini_Protoboard_Shield1.X9-Y11
  N1: WeMos_D1_Mini1.D1, WeMos_D1_Mini_OLED_Shield1.D1, WeMos_D1_Mini_Protoboard_Shield1.D1
  N2: WeMos_D1_Mini1.D2, WeMos_D1_Mini_OLED_Shield1.D2, WeMos_D1_Mini_Protoboard_Shield1.D2
  N3: WeMos_D1_Mini1.D5, WeMos_D1_Mini_Micro_SD_Shield1.D5
  N4: WeMos_D1_Mini1.D6, WeMos_D1_Mini_Micro_SD_Shield1.D6
  N5: WeMos_D1_Mini1.D7, WeMos_D1_Mini_Micro_SD_Shield1.D7
  N6: WeMos_D1_Mini1.D8, WeMos_D1_Mini_Micro_SD_Shield1.D8
  N7: WeMos_D1_Mini1.G, WeMos_D1_Mini_OLED_Shield1.G, WeMos_D1_Mini_Protoboard_Shield1.X9-Y10
  N8: WeMos_D1_Mini1.RST, WeMos_D1_Mini_Micro_SD_Shield1.RST, WeMos_D1_Mini_OLED_Shield1.RST, WeMos_D1_Mini_Protoboard_Shield1.RST

notes:
  RTC Shield
